// Digital circuit cpu.dig as structural Verilog
module cpu (
  input  CLK,
  input  CLK_en,
  output [3:0] PC
);

  wire CLK_t;
  wire [3:0] add_1_s, alu_1_alu_out, multiplexer_1_out, registerfile_1_da, registerfile_1_db;
  wire [6:0] ramsingleport_1_d;

  Register #(.Bits(4)) register_1 (.D(add_1_s), .C(CLK_t), .en(1'b1), .Q(PC));
  RAMSinglePort #(.AddrBits(4), .isProgramMemory("true"), .Bits(7)) ramsingleport_1 (
    .A(PC), .str(1'b0), .C(CLK_t), .ld(1'b1), .D(ramsingleport_1_d));
  Add #(.Bits(4)) add_1 (.a(PC), .b(4'b0001), .c_i(1'b0), .s(add_1_s));  // open: c_o
  RegisterFile #(.Bits(4)) registerfile_1 (
    .Din(alu_1_alu_out), .we(1'b1), .Rw(ramsingleport_1_d[3:2]), .C(CLK_t), .Ra(ramsingleport_1_d[1:0]),
    .Rb(ramsingleport_1_d[3:2]), .Da(registerfile_1_da), .Db(registerfile_1_db));
  and and_1 (CLK_t, CLK, CLK_en);
  Multiplexer #(.Bits(4)) multiplexer_1 (
    .sel(ramsingleport_1_d[6]), .in_0(registerfile_1_da), .in_1({2'b00, ramsingleport_1_d[1:0]}),
    .out(multiplexer_1_out));
  alu alu_1 (
    .src(multiplexer_1_out), .dest(registerfile_1_db), .alu_sel(ramsingleport_1_d[5:4]),
    .alu_out(alu_1_alu_out));

  // Notes on the sheet:
  //   NPC
  //   Program Mem
  //   Reg
  //   File
  //   ISA:
  //   add  dest, src
  //   sub  dest, src
  //   mult dest, src
  //   div  dest, src
  //   addi dest, imm
  //   subi dest, imm
  //   r-type: 0x0__
  //   add  0x000
  //   sub  0x001
  //   mult 0x010
  //   div  0x011
  //   i-type: 0x1__
  //   addi 0x100
  //   subi 0x101
  //   registers:
  //   r0 0x00
  //   r1 0x01
  //   r2 0x10
  //   r3 0x11
  //   immediate:
  //   2 bit values
endmodule
