// Digital circuit alu.dig as structural Verilog
module alu (
  input  [3:0] src,
  input  [3:0] dest,
  input  [1:0] alu_sel,
  output [3:0] alu_out
);

  wire [3:0] add_1_s, div_1_q, sub_1_s;
  wire [7:0] mul_1_mul;

  Add #(.Bits(4)) add_1 (.a(src), .b(dest), .c_i(1'b0), .s(add_1_s));  // open: c_o
  Sub #(.Bits(4)) sub_1 (.a(dest), .b(src), .c_i(1'b0), .s(sub_1_s));  // open: c_o
  Mul #(.Bits(4)) mul_1 (.a(src), .b(dest), .mul(mul_1_mul));
  Div #(.Bits(4)) div_1 (.a(dest), .b(src), .q(div_1_q));  // open: r
  Multiplexer #(.Selector_Bits(2), .Bits(4)) multiplexer_1 (
    .sel(alu_sel), .in_0(add_1_s), .in_1(sub_1_s), .in_2(mul_1_mul[3:0]), .in_3(div_1_q), .out(alu_out));
endmodule
